# Fritzing sketch ESP8266_DHT22 (saved by Fritzing 0.9.2b)
circuit board: 8.46667cm x 5.64444cm
stripboards: 1

parts:
  R1 = Resistor [tolerance=±5% resistance=10k package=THT]
  S2 = Pushbutton [package="[THT]"]
  S1 = Pushbutton [package="[THT]"]
  DHT1 = DHT22 Humidity and Temperature Sensor
  J1 = female pin header, 6 pins [form="♀ (female)"]
  R2 = Resistor [tolerance=±5% resistance=10k package=THT]
  U1 = ESP8266 WiFi Module [part_number=ESP8266]
  R3 = Resistor [tolerance=±5% resistance=10k package=THT]

nets:
  VDD: R1.Pin_0, DHT1.VDD, R2.Pin_0, U1.VCC, R3.Pin_0
  N1: R1.Pin_1, S1.Pin_1, S1.Pin_2, U1.RST
  N2: S2.Pin_1, S2.Pin_2, U1.GPIO_0
  GND: S2.Pin_3, S2.Pin_4, S1.Pin_3, S1.Pin_4, DHT1.NULL, DHT1.GND, J1.pin1, U1.GND
  N3: DHT1.DATA, R2.Pin_1, U1.GPIO_2
  N4: J1.pin4, U1.RXD
  N5: J1.pin5, U1.TXD
  N6: U1.CH_PD, R3.Pin_1

custom parts:
  ESP8266 WiFi Module: Generic WiFi Module based on the ESP8266 with onboard PCB antenna and UART communications
